// Logisim project CPU_microprocessor.circ as structural Verilog: 15 circuits, main circuit main
module main (
  input  in_1,
  input  in_2,
  input  in_3,
  output out_4,
  output out_5,
  output out_6,
  output out_7,
  output out_8,
  output out_9
);

  wire ac_15_t, AC_LD, and_2_out, and_3_out, and_4_out, and_6_out, and_7_out, and_8_out, and_30_out,
       and_31_out, and_41_out, and_42_out, B0, B1, B2, B3, B4, B5, B6, B7, B8, B9, B10, B11, Clk,
       common_bus_1_e_out, D0, D0T4, D0T5, D1, D1T4, D1T5, D2, D2T4, D2T5, D3, D3T4, D4, D4T4, D5, D5T4,
       D5T5, D6, D6T4, D6T5, D6T6, D7, E, I, ISZ, not_1_out, not_2_out, not_3_out, not_4_out, not_5_out,
       not_6_out, not_7_out, or_1_out, or_2_out, or_3_out, or_5_out, or_8_out, or_13_out, or_19_out,
       or_20_out, PC_INR, r, R0, R1, R2, R3, R4, R5, R6, R7, R8, R9, R10, R11, SC_inr, SZA, T0, T1, T2, T3,
       T4, T5, T6, WR_EN, x1, x2, x3, x4, x5, x7;
  wire [1:0] E_sel;
  wire [2:0] ALU, Source;
  wire [14:12] IR;
  wire [15:0] AC, common_bus_1_ar, common_bus_1_pc, DR;

  Clock clock_1 (.out(Clk));
  Sequence_counter sequence_counter_1 (
    .CLK(Clk), .INR(SC_inr), .CLR(out_9), .T0(T0), .T1(T1), .T2(T2), .T3(T3), .T4(T4), .T5(T5), .T6(T6));
  Common_bus common_bus_1 (
    .WR_EN(WR_EN), .RD_EN(x7), .CLK(Clk), .Source(Source), .AR_INR(out_4), .AR_CLR(1'b0), .AR_LD(out_5),
    .PC_INR(PC_INR), .PC_CLR(in_2), .PC_LD(out_6), .DR_INR(out_8), .DR_CLR(in_3), .DR_LD(out_7), .AC_INR(R5),
    .AC_CLR(R11), .AC_LD(AC_LD), .ALU_select(ALU), .IR_LD(T1), .TR_INR(1'b0), .TR_CLR(1'b0), .TR_LD(1'b0),
    .E_comp(R9), .E_CLR(R10), .E_LD(D1T5), .E_SELECT(E_sel), .AR(common_bus_1_ar), .PC(common_bus_1_pc),
    .DR(DR), .AC(AC), .IR({I, IR, B11, B10, B9, B8, B7, B6, B5, B4, B3, B2, B1, B0}),
    .E_out(common_bus_1_e_out));
  // Probe on common_bus_1_ar
  not not_1 (not_1_out, common_bus_1_e_out);
  // Probe on common_bus_1_e_out
  // Probe on common_bus_1_pc
  and and_1 (E, not_1_out, R1);
  or or_1 (or_1_out, D3, D4);
  // Probe on DR
  Decoder #(.enable("false"), .select(3)) decoder_1 (
    .out0(D0), .out1(D1), .out2(D2), .out3(D3), .out4(D4), .out5(D5), .out6(D6), .out7(D7), .sel(IR));
  // Probe on AC
  // Probe on {I, IR, B11, B10, B9, B8, B7, B6, B5, B4, B3, B2, B1, B0}
  or or_2 (or_2_out, D0, D1, D2, D5);
  or or_3 (or_3_out, r, R0);
  and and_2 (and_2_out, T6, D6);
  and and_3 (and_3_out, T5, or_2_out);
  and and_4 (and_4_out, T4, or_1_out);
  or or_4 (out_9, and_3_out, and_2_out, and_4_out, or_3_out);
  or or_5 (or_5_out, D3, D5);
  and and_5 (out_4, D5, T4);
  not not_2 (not_2_out, D7);
  and and_6 (and_6_out, I, not_2_out, T3);
  or or_6 (PC_INR, T1, R1, R2, R3, R4, E, ISZ, SZA, ac_15_t);
  or or_7 (out_6, D4T4, D5T5);
  or or_8 (or_8_out, D0, D1, D2, D6);
  and and_7 (and_7_out, or_5_out, T4);
  and and_8 (and_8_out, T6, D6);
  or or_9 (out_5, T0, T2, and_6_out);
  and and_9 (out_7, or_8_out, T4);
  and and_10 (out_8, D6, T5);
  or or_10 (AC_LD, D1T5, D6T5, D2T5, R6, R7, R8);
  or or_11 (WR_EN, and_7_out, and_8_out);
  and and_11 (R0, r, B0);
  and and_12 (R1, r, B1);
  and and_13 (R2, r, B2);
  and and_14 (R3, r, B3);
  and and_15 (R4, r, B4);
  and and_16 (R5, r, B5);
  and and_17 (R7, r, B7);
  Start_switch start_switch_1 (.Start(in_1), .rst(out_9), .Clk(Clk), .SC_inr(SC_inr));
  Bus_selection bus_selection_1 (.x1(x1), .x2(x2), .x3(x3), .x4(x4), .x5(x5), .x6(1'b0), .x7(x7), .Source(Source));
  // Probe on Source
  ALU_selection alu_selection_1 (.A1(D0T5), .A2(D1T5), .A3(D2T5), .A4(R9), .A5(R7), .A6(R6), .Alu_select(ALU));
  // Probe on ALU
  E_selection e_selection_1 (.E1(D1T5), .E2(R7), .E3(R6), .AB(E_sel));
  // Probe on E_sel
  and and_18 (R6, r, B6);
  and and_19 (R8, r, B8);
  and and_20 (R9, r, B9);
  and and_21 (R10, r, B10);
  and and_22 (R11, r, B11);
  not not_3 (not_3_out, I);
  not not_4 (not_4_out, D7);
  and and_23 (r, D7, not_3_out, T3);
  and and_24 (D0T4, D0, T4);
  and and_25 (D0T5, D0, T5);
  and and_26 (D1T4, D1, T4);
  and and_27 (D2T4, D2, T4);
  and and_28 (D2T5, D2, T5);
  and and_29 (D1T5, D1, T5);
  or or_12 (x5, T2, 1'b0);
  or or_13 (or_13_out, D0, D1, D2, D6);
  or or_14 (x1, D5T5, D4T4);
  or or_15 (x2, D5T4, T0);
  or or_16 (x3, D0T5, D1T5, D2T5);
  or or_17 (x4, D0T5, D1T5, D3T4);
  and and_30 (and_30_out, or_13_out, T4);
  and and_31 (and_31_out, not_4_out, I, T3);
  or or_18 (x7, and_30_out, and_31_out, T1);
  and and_32 (D3T4, D3, T4);
  and and_33 (D4T4, D4, T4);
  and and_34 (D5T4, D5, T4);
  and and_35 (D5T5, D5, T5);
  and and_36 (D6T4, D6, T4);
  and and_37 (D6T5, D6, T5);
  and and_38 (D6T6, D6, T6);
  or or_19 (or_19_out, AC[15], AC[14], AC[13], AC[12], AC[11], AC[10], AC[9], AC[8], AC[7], AC[6], AC[5], AC[4], AC[3], AC[2], AC[1], AC[0]);
  or or_20 (or_20_out, DR[15], DR[14], DR[13], DR[12], DR[11], DR[10], DR[9], DR[8], DR[7], DR[6], DR[5], DR[4], DR[3], DR[2], DR[1], DR[0]);
  not not_5 (not_5_out, or_19_out);
  not not_6 (not_6_out, or_20_out);
  not not_7 (not_7_out, AC[15]);
  and and_39 (SZA, not_5_out, R2);
  and and_40 (ISZ, not_6_out, D6T6);
  and and_41 (and_41_out, R3, AC[15]);
  and and_42 (and_42_out, not_7_out, R4);
  or or_21 (ac_15_t, and_41_out, and_42_out);

  // Other names for the same wires on the sheet: AC_15 = AC[15]; AR_INR = out_4; AR_LD = out_5; clr = in_2;
  //   DR_INR = out_8; DR_LD = out_7; IR (some bits) = {I, B11, B10, B9, B8, B7, B6, B5, B4, B3, B2, B1, B0};
  //   Op0 = IR[12]; Op1 = IR[13]; Op2 = IR[14]; PC_LD = out_6; rst = out_9; Start = in_1
endmodule

module Common_bus (
  input  WR_EN,
  input  RD_EN,
  input  CLK,
  input  [2:0] Source,
  input  AR_INR,
  input  AR_CLR,
  input  AR_LD,
  input  PC_INR,
  input  PC_CLR,
  input  PC_LD,
  input  DR_INR,
  input  DR_CLR,
  input  DR_LD,
  input  AC_INR,
  input  AC_CLR,
  input  AC_LD,
  input  [2:0] ALU_select,
  input  IR_LD,
  input  TR_INR,
  input  TR_CLR,
  input  TR_LD,
  input  E_comp,
  input  E_CLR,
  input  E_LD,
  input  [1:0] E_SELECT,
  output [15:0] AR,
  output [15:0] PC,
  output [15:0] DR,
  output [15:0] AC,
  output [15:0] IR,
  output E_out
);

  wire Cout, multiplexer_1_out;
  wire [11:0] address_register_1_address;
  wire [15:0] alu_1_alu_out, multiplexer_2_out, ram_1_dout, temporary_register_1_dataout;

  // Probe on AC
  // Probe on DR
  ALU alu_1 (.AC(AC), .DR(DR), .ALU_SELECT(ALU_select), .EL(E_out), .ER(E_out), .ALU_OUT(alu_1_alu_out), .Cout(Cout));
  Multiplexer #(.select(2)) multiplexer_1 (
    .in1(Cout), .in2(AC[0]), .in3(AC[15]), .out(multiplexer_1_out), .sel(E_SELECT));  // open: in0
  // Probe on address_register_1_address
  RAM #(.addrWidth(12), .asyncread("true"), .dataWidth(16)) ram_1 (
    .addr(address_register_1_address), .we(WR_EN), .oe(RD_EN), .clk(CLK), .din(multiplexer_2_out),
    .dout(ram_1_dout));
  Address_register address_register_1 (
    .INR(AR_INR), .CLR(AR_CLR), .LD(AR_LD), .CLK(CLK), .Datain(multiplexer_2_out),
    .Address(address_register_1_address), .Dataout(AR));
  Program_counter program_counter_1 (
    .INR(PC_INR), .CLR(PC_CLR), .LD(PC_LD), .CLK(CLK), .Datain(multiplexer_2_out), .Dataout(PC));
  Data_register data_register_1 (
    .INR(DR_INR), .CLR(DR_CLR), .CLK(CLK), .LOAD(DR_LD), .Datain(multiplexer_2_out), .Dataout(DR));
  Accumulator accumulator_1 (.INR(AC_INR), .CLR(AC_CLR), .CLK(CLK), .LOAD(AC_LD), .Datain(alu_1_alu_out), .Dataout(AC));
  Instruction_register instruction_register_1 (.Datain(multiplexer_2_out), .CLK(CLK), .LOAD(IR_LD), .Dataout(IR));
  Temporary_register temporary_register_1 (
    .INR(TR_INR), .CLR(TR_CLR), .CLK(CLK), .LOAD(TR_LD), .Datain(multiplexer_2_out),
    .Dataout(temporary_register_1_dataout));
  E_Flipflop e_flipflop_1 (
    .Com_E(E_comp), .CLR(E_CLR), .CLK(CLK), .LOAD(E_LD), .Datain(multiplexer_1_out), .E_ff_op(E_out));
  Multiplexer #(.select(3), .width(16)) multiplexer_2 (
    .in1(AR), .in2(PC), .in3(DR), .in4(AC), .in5(IR), .in6(temporary_register_1_dataout), .in7(ram_1_dout),
    .out(multiplexer_2_out), .sel(Source));  // open: in0
  // Probe on multiplexer_2_out

  // Other names for the same wires on the sheet: AC_0 = AC[0]; AC_out[15:0] = AC; AC_15 = AC[15]; DR_out[15:0] = DR;
  //   E_ff = E_out
endmodule

module Address_register (
  input  INR,
  input  CLR,
  input  LD,
  input  CLK,
  input  [15:0] Datain,
  output [11:0] Address,
  output [15:0] Dataout
);

  wire [11:0] adder_1_out, multiplexer_1_out, multiplexer_2_out, multiplexer_3_out;

  Adder #(.width(12)) adder_1 (.a(Address), .b(12'h1), .out(adder_1_out));  // open: cin, cout
  Multiplexer #(.width(12)) multiplexer_1 (.in0(Address), .in1(adder_1_out), .out(multiplexer_1_out), .sel(INR));
  Multiplexer #(.width(12)) multiplexer_2 (
    .in0(multiplexer_1_out), .in1({12{1'b0}}), .out(multiplexer_2_out), .sel(CLR));
  Multiplexer #(.width(12)) multiplexer_3 (
    .in0(multiplexer_2_out), .in1(Datain[11:0]), .out(multiplexer_3_out), .sel(LD));
  Register #(.width(12)) register_1 (.D(multiplexer_3_out), .clk(CLK), .Q(Address));  // open: en, clr

  assign Dataout = {4'b0000, Address};
endmodule

module Program_counter (
  input  INR,
  input  CLR,
  input  LD,
  input  CLK,
  input  [15:0] Datain,
  output [15:0] Dataout
);

  wire [11:0] adder_1_out, multiplexer_1_out, multiplexer_2_out, multiplexer_3_out;

  Adder #(.width(12)) adder_1 (.a(Dataout[11:0]), .b(12'h1), .out(adder_1_out));  // open: cin, cout
  Multiplexer #(.width(12)) multiplexer_1 (.in0(Dataout[11:0]), .in1(adder_1_out), .out(multiplexer_1_out), .sel(INR));
  Multiplexer #(.width(12)) multiplexer_2 (
    .in0(multiplexer_1_out), .in1({12{1'b0}}), .out(multiplexer_2_out), .sel(CLR));
  Multiplexer #(.width(12)) multiplexer_3 (
    .in0(multiplexer_2_out), .in1(Datain[11:0]), .out(multiplexer_3_out), .sel(LD));
  Register #(.width(12)) register_1 (.D(multiplexer_3_out), .clk(CLK), .Q(Dataout[11:0]));  // open: en, clr

  assign Dataout[15:12] = 4'b0000;
endmodule

module Data_register (
  input  INR,
  input  CLR,
  input  CLK,
  input  LOAD,
  input  [15:0] Datain,
  output [15:0] Dataout
);

  wire [15:0] adder_1_out, multiplexer_1_out, multiplexer_2_out, multiplexer_3_out;

  Adder #(.width(16)) adder_1 (.a(Dataout), .b(16'h1), .out(adder_1_out));  // open: cin, cout
  Multiplexer #(.width(16)) multiplexer_1 (.in0(Dataout), .in1(adder_1_out), .out(multiplexer_1_out), .sel(INR));
  Multiplexer #(.width(16)) multiplexer_2 (
    .in0(multiplexer_1_out), .in1({16{1'b0}}), .out(multiplexer_2_out), .sel(CLR));
  Multiplexer #(.width(16)) multiplexer_3 (.in0(multiplexer_2_out), .in1(Datain), .out(multiplexer_3_out), .sel(LOAD));
  Register #(.width(16)) register_1 (.D(multiplexer_3_out), .clk(CLK), .Q(Dataout));  // open: en, clr
endmodule

module Accumulator (
  input  INR,
  input  CLR,
  input  CLK,
  input  LOAD,
  input  [15:0] Datain,
  output [15:0] Dataout
);

  wire [15:0] adder_1_out, multiplexer_1_out, multiplexer_2_out, multiplexer_3_out;

  Adder #(.width(16)) adder_1 (.a(Dataout), .b(16'h1), .out(adder_1_out));  // open: cin, cout
  Multiplexer #(.width(16)) multiplexer_1 (.in0(Dataout), .in1(adder_1_out), .out(multiplexer_1_out), .sel(INR));
  Multiplexer #(.width(16)) multiplexer_2 (
    .in0(multiplexer_1_out), .in1({16{1'b0}}), .out(multiplexer_2_out), .sel(CLR));
  Multiplexer #(.width(16)) multiplexer_3 (.in0(multiplexer_2_out), .in1(Datain), .out(multiplexer_3_out), .sel(LOAD));
  Register #(.width(16)) register_1 (.D(multiplexer_3_out), .clk(CLK), .Q(Dataout));  // open: en, clr
endmodule

module Instruction_register (
  input  [15:0] Datain,
  input  CLK,
  input  LOAD,
  output [15:0] Dataout
);

  wire [15:0] multiplexer_1_out;

  Multiplexer #(.width(16)) multiplexer_1 (.in0(Dataout), .in1(Datain), .out(multiplexer_1_out), .sel(LOAD));
  Register #(.width(16)) register_1 (.D(multiplexer_1_out), .clk(CLK), .Q(Dataout));  // open: en, clr
endmodule

module Temporary_register (
  input  INR,
  input  CLR,
  input  CLK,
  input  LOAD,
  input  [15:0] Datain,
  output [15:0] Dataout
);

  wire [15:0] adder_1_out, multiplexer_1_out, multiplexer_2_out, multiplexer_3_out;

  Adder #(.width(16)) adder_1 (.a(Dataout), .b(16'h1), .out(adder_1_out));  // open: cin, cout
  Multiplexer #(.width(16)) multiplexer_1 (.in0(Dataout), .in1(adder_1_out), .out(multiplexer_1_out), .sel(INR));
  Multiplexer #(.width(16)) multiplexer_2 (
    .in0(multiplexer_1_out), .in1({16{1'b0}}), .out(multiplexer_2_out), .sel(CLR));
  Multiplexer #(.width(16)) multiplexer_3 (.in0(multiplexer_2_out), .in1(Datain), .out(multiplexer_3_out), .sel(LOAD));
  Register #(.width(16)) register_1 (.D(multiplexer_3_out), .clk(CLK), .Q(Dataout));  // open: en, clr
endmodule

module ALU (
  input  [15:0] AC,
  input  [15:0] DR,
  input  [2:0] ALU_SELECT,
  input  EL,
  input  ER,
  output [15:0] ALU_OUT,
  output Cout
);

  wire [15:0] adder_1_out, and_1_out, not_1_out;

  assign and_1_out = DR & AC;  // AND_Gate and_1, 16 bits wide
  Adder #(.width(16)) adder_1 (.a(DR), .b(AC), .out(adder_1_out), .cout(Cout));  // open: cin
  assign not_1_out = ~AC;  // NOT_Gate not_1, 16 bits wide
  Multiplexer #(.select(3), .width(16)) multiplexer_1 (
    .in1(and_1_out), .in2(adder_1_out), .in3(DR), .in4(not_1_out), .in5({ER, AC[15:1]}),
    .in6({AC[14:0], EL}), .out(ALU_OUT), .sel(ALU_SELECT));  // open: in0, in7

  // Notes on the sheet:
  //   Right
  //   Left
endmodule

module E_Flipflop (
  input  Com_E,
  input  CLR,
  input  CLK,
  input  LOAD,
  input  Datain,
  output E_ff_op
);

  wire multiplexer_1_out, multiplexer_2_out, multiplexer_3_out, not_1_out;

  not not_1 (not_1_out, E_ff_op);
  Multiplexer multiplexer_1 (.in0(E_ff_op), .in1(not_1_out), .out(multiplexer_1_out), .sel(Com_E));
  Multiplexer multiplexer_2 (.in0(multiplexer_1_out), .in1(1'b0), .out(multiplexer_2_out), .sel(CLR));
  Multiplexer multiplexer_3 (.in0(multiplexer_2_out), .in1(Datain), .out(multiplexer_3_out), .sel(LOAD));
  D_Flip_Flop d_ff_1 (.D(multiplexer_3_out), .clk(CLK), .Q(E_ff_op));  // open: Qn, preset, reset
endmodule

module Sequence_counter (
  input  CLK,
  input  INR,
  input  CLR,
  output T0,
  output T1,
  output T2,
  output T3,
  output T4,
  output T5,
  output T6
);

  wire [2:0] adder_1_out, multiplexer_1_out, multiplexer_2_out, register_1_q;

  Adder #(.width(3)) adder_1 (.a(register_1_q), .b(3'b001), .out(adder_1_out));  // open: cin, cout
  Multiplexer #(.width(3)) multiplexer_1 (.in0(register_1_q), .in1(adder_1_out), .out(multiplexer_1_out), .sel(INR));
  Multiplexer #(.width(3)) multiplexer_2 (.in0(multiplexer_1_out), .in1(3'b000), .out(multiplexer_2_out), .sel(CLR));
  Register #(.width(3)) register_1 (.D(multiplexer_2_out), .clk(CLK), .Q(register_1_q));  // open: en, clr
  Decoder #(.select(3)) decoder_1 (
    .out1(T0), .out2(T1), .out3(T2), .out4(T3), .out5(T4), .out6(T5), .out7(T6), .sel(register_1_q));  // open: out0, en
endmodule

module Start_switch (
  input  Start,
  input  rst,
  input  Clk,
  output SC_inr
);

  wire and_1_out, not_1_out, or_1_out;

  not not_1 (not_1_out, rst);
  and and_1 (and_1_out, not_1_out, SC_inr);
  or or_1 (or_1_out, Start, and_1_out);
  D_Flip_Flop d_ff_1 (.D(or_1_out), .clk(Clk), .Q(SC_inr));  // open: Qn, preset, reset
endmodule

module Bus_selection (
  input  x1,
  input  x2,
  input  x3,
  input  x4,
  input  x5,
  input  x6,
  input  x7,
  output [2:0] Source
);

  or or_1 (Source[0], x1, x3, x5, x7);
  or or_2 (Source[1], x2, x3, x6, x7);
  or or_3 (Source[2], x4, x5, x6, x7);

  // Notes on the sheet:
  //   x1=AR
  //   x2=PC
  //   x3=DR
  //   x4=AC
  //   x5=IR
  //   x6=TR
  //   x7=memory
endmodule

module ALU_selection (
  input  A1,
  input  A2,
  input  A3,
  input  A4,
  input  A5,
  input  A6,
  output [2:0] Alu_select
);

  or or_1 (Alu_select[0], A1, A3, A5);
  or or_2 (Alu_select[1], A2, A3, A6);
  or or_3 (Alu_select[2], A4, A5, A6);

  // Notes on the sheet:
  //   A1=AND
  //   A2=ADD
  //   A3=LOAD
  //   A4=COMPLEMET
  //   A5=SHIFT RIGHT
  //   A6=SHIFT LEFT
endmodule

module E_selection (
  input  E1,
  input  E2,
  input  E3,
  output [1:0] AB
);

  or or_1 (AB[0], E1, E3);
  or or_2 (AB[1], E2, E3);

  // Other names for the same wires on the sheet: x1 = E1; x2 = E2; x3 = E3

  // Notes on the sheet:
  //   B
  //   A
endmodule
